# Fritzing sketch fire_detection_robot (saved by Fritzing 1.0.4)
breadboards: 1

parts:
  Εξάρτημα1 = Arduino Mega 2560 (Rev3)
  HC-SR04_Sensor_Left = HC-SR04 Ultrasonic Distance Sensor
  HC-SR04_Sensor_Front = HC-SR04 Ultrasonic Distance Sensor
  HC-SR04_Sensor_Right = HC-SR04 Ultrasonic Distance Sensor
  MQ-2 = MQ-2 Gas Sensor  # not connected
  L298N = L298_BRIDGE_DRIVER [package=powerso20]  # not connected
  DC_Motor_Left = gear-motor  # not connected
  DC_Motor_Right = gear-motor  # not connected
  GY-NEO6MV3 = SUP500F [package=sup500f]  # not connected
  SX1278 = Osoyoo SX1278-ra-02  # not connected
  ANT1 = Antenna  # not connected
  QMC5883L = QMC5883L - Triple Axis Magnetometer Breakout  # not connected
  DC-DC_Converter_5V = RioRand LM2596  # not connected
  DC-DC_Converter_6V = RioRand LM2596  # not connected
  J1 = Basic Servo  # not connected

nets:
  N1: Εξάρτημα1.D2_PWM, HC-SR04_Sensor_Front.TRIG
  N2: Εξάρτημα1.D3_PWM, HC-SR04_Sensor_Front.ECHO
  N3: Εξάρτημα1.D4_PWM, HC-SR04_Sensor_Right.TRIG
  N4: Εξάρτημα1.D5_PWM, HC-SR04_Sensor_Right.ECHO
  N5: Εξάρτημα1.D6_PWM, HC-SR04_Sensor_Left.TRIG
  N6: Εξάρτημα1.D7_PWM, HC-SR04_Sensor_Left.ECHO

notes:
  GND:Black
  VCC: Red
  RX: Yellow
  TX: Green

custom parts:
  MQ-2 Gas Sensor: MQ-2 Gas Sensor module of ZHIYU Sensor Kit
  Osoyoo SX1278-ra-02: Osoyoo Long Distance wireless transceiver Uart LoRa Module.
